# Fritzing sketch MH_CD42 Power Board USB3 Female Out (saved by Fritzing 0.9.6b)
circuit board: 5.58781cm x 3.15601cm
breadboards: 1

parts:
  J1 = female pin header, 6 pins [form="♀ (female)"]
  BAT = Header 2 [package=jst-2-pth]
  BAT_PWR = Toggle Switch [package=THT]
  BAT_LVL = female pin header, 2 pins [form="♀ (female)"]
  10K = Resistor [tolerance=±5% resistance=10k power=0.25 package="1206 [SMD]"]
  33K = Resistor [tolerance=±5% resistance=33k power=0.25 package="1206 [SMD]"]
  1K = Resistor [tolerance=±5% resistance=1k power=0.25 package="1206 [SMD]"]
  5V = female pin header, 2 pins [form="♀ (female)"]
  0V = female pin header, 2 pins [form="♀ (female)"]
  USB_B_IN = Mini-USB _B_ connector with 5th pin broken out. [package=usb-minib]
  X1 = USB Connectors [package="usb3 - female"]

nets:
  N1: J1.pin1, 5V.pin1, 5V.pin2, X1.VBUS
  N2: J1.pin2, 33K.Pin_1, 0V.pin1, 0V.pin2, X1.GND
  N3: J1.pin3, BAT.2, BAT_PWR.L1
  N4: J1.pin4, BAT.1
  N5: J1.pin5, USB_B_IN.GND
  N6: J1.pin6, USB_B_IN.VBUS
  N7: BAT_PWR.COM, 10K.Pin_0
  N8: BAT_LVL.pin1, BAT_LVL.pin2, 1K.Pin_1
  N9: 10K.Pin_1, 33K.Pin_0, 1K.Pin_0

notes:
  MH-CD42
  OUT 5V
  GND
  BAT+
  V IN
  +
  MH-CD42 Power Board
  github.com/GOTO-GOSUB
  PI SAFE
  ON / OFF
